# Fritzing sketch Tamis (saved by Fritzing 0.9.2b)

parts:
  J1 = Basic Force Sensing Resistor (FSR) [package=THT]
  Composant1 = Arduino Uno (Rev3)
  Composant2 = Triple Axis Accelerometer Breakout - ADXL335
  R1 = Resistor [tolerance=±5% resistance=11k package=THT]

nets:
  N1: J1.pin_0, Composant1.A0, R1.Pin_0
  GND: J1.pin_1, Composant1.GND, Composant2.GND
  N2: Composant1.A1, Composant2.ZOUT
  N3: Composant1.A2, Composant2.YOUT
  N4: Composant1.A3, Composant2.XOUT
  5V: Composant1.5V, Composant2.VCC, R1.Pin_1
